// Logisim project CPU.circ as structural Verilog: 23 circuits, main circuit PC_8_BIT
module PC_8_BIT (
  input  Select,
  input  Pulse,
  input  PROGRAMMING,
  input  RESET
);

  wire ALU_carry, and_1_out, and_2_out, and_3_out, and_4_out, bcdconverter8bit_1_hundreds0,
       bcdconverter8bit_1_hundreds1, bcdconverter8bit_1_negative, bcdconverter8bit_1_ones0,
       bcdconverter8bit_1_ones1, bcdconverter8bit_1_ones2, bcdconverter8bit_1_ones3,
       bcdconverter8bit_1_tens0, bcdconverter8bit_1_tens1, bcdconverter8bit_1_tens2,
       bcdconverter8bit_1_tens3, CLOCK_output, decoder7segment_1_a, decoder7segment_1_b, decoder7segment_1_c,
       decoder7segment_1_d, decoder7segment_1_e, decoder7segment_1_f, decoder7segment_1_g,
       decoder7segment_2_a, decoder7segment_2_b, decoder7segment_2_c, decoder7segment_2_d,
       decoder7segment_2_e, decoder7segment_2_f, decoder7segment_2_g, decoder7segment_3_a,
       decoder7segment_3_b, decoder7segment_3_c, decoder7segment_3_d, decoder7segment_3_e,
       decoder7segment_3_f, decoder7segment_3_g, demux3x8_1_y5, FLAGS_REGISTER_cf, FLAGS_REGISTER_zf,
       INSTRUCTION_COUNTER_q0, INSTRUCTION_COUNTER_q1, INSTRUCTION_COUNTER_q2, instruction_rom_1_ain,
       instruction_rom_1_aout, instruction_rom_1_bin, instruction_rom_1_bout, instruction_rom_1_ce,
       instruction_rom_1_co, instruction_rom_1_cs, instruction_rom_1_display, instruction_rom_1_e0,
       instruction_rom_1_fi, instruction_rom_1_hlt, instruction_rom_1_irload, instruction_rom_1_irout,
       instruction_rom_1_jmp, instruction_rom_1_mi, instruction_rom_1_s1_2, instruction_rom_1_s2_2,
       instruction_rom_1_signed, instruction_rom_1_su, instruction_rom_1_wr, MANUALWRITE_out,
       masterreset_1_reset, masterreset_1_stepreset, nor_1_out, not_1_out, not_2_out, or_1_out, RESET_out;
  wire [3:0] ADD_MUX_out, MANUALADDRESS_sw4, MANUALDATA_sw4, MANUALDATA_sw8, MEM_REG_q,
       octalbustransceiver_1_q, octalbustransceiver_1_q_2, PROGRAM_COUNTER_q0;
  wire [7:0] ADD_MUX_3_out, dreg8bit_1_q, IREG_q, octalbustransceiver_3_q, octalbustransceiver_4_q, RAM_o,
       REG_A_q, REG_B_q;
  wire [7:4] undriven;

  DipSwitch #(.number(4)) MANUALADDRESS (
    .sw1(MANUALADDRESS_sw4[3]), .sw2(MANUALADDRESS_sw4[2]), .sw3(MANUALADDRESS_sw4[1]),
    .sw4(MANUALADDRESS_sw4[0]));
  or or_1 (or_1_out, and_1_out, and_2_out);
  and and_1 (and_1_out, PROGRAMMING, MANUALWRITE_out);
  Button MANUALWRITE (.out(MANUALWRITE_out));
  MEMREG4BIT MEM_REG (
    .CLEAR(masterreset_1_reset), .LOAD(instruction_rom_1_mi), .D(octalbustransceiver_1_q),
    .CLOCK(CLOCK_output), .Q(MEM_REG_q));
  RAM16BYTE RAM (
    .A(ADD_MUX_out), .RESET(RESET), .D(ADD_MUX_3_out), .WR(or_1_out), .CS(instruction_rom_1_cs), .O(RAM_o));
  and and_2 (and_2_out, CLOCK_output, instruction_rom_1_wr);
  DipSwitch MANUALDATA (
    .sw1(MANUALDATA_sw4[3]), .sw2(MANUALDATA_sw4[2]), .sw3(MANUALDATA_sw4[1]), .sw4(MANUALDATA_sw4[0]),
    .sw5(MANUALDATA_sw8[3]), .sw6(MANUALDATA_sw8[2]), .sw7(MANUALDATA_sw8[1]), .sw8(MANUALDATA_sw8[0]));
  DREG8BIT IREG (
    .CLEAR(masterreset_1_reset), .LOAD(instruction_rom_1_irload),
    .D({octalbustransceiver_1_q_2, octalbustransceiver_1_q}), .PAR(1'b0), .CLOCK(CLOCK_output), .Q(IREG_q));  // open: PD
  MUX2X1 ADD_MUX (.A(MANUALADDRESS_sw4), .B(MEM_REG_q), .Select(PROGRAMMING), .Out(ADD_MUX_out));
  not not_1 (not_1_out, or_1_out);
  LED led_1 (.in(RAM_o[6]));
  LED led_2 (.in(RAM_o[7]));
  LED led_3 (.in(RAM_o[5]));
  LED led_4 (.in(IREG_q[6]));
  LED led_5 (.in(IREG_q[7]));
  LED led_6 (.in(IREG_q[5]));
  LED led_7 (.in(ADD_MUX_out[2]));
  LED led_8 (.in(ADD_MUX_out[3]));
  LED led_9 (.in(RAM_o[3]));
  LED led_10 (.in(RAM_o[1]));
  LED led_11 (.in(RAM_o[4]));
  LED led_12 (.in(RAM_o[2]));
  LED led_13 (.in(IREG_q[3]));
  LED led_14 (.in(IREG_q[2]));
  LED led_15 (.in(IREG_q[1]));
  LED led_16 (.in(IREG_q[4]));
  INSTRUCTION_ROM instruction_rom_1 (
    .CF(FLAGS_REGISTER_cf), .ZF(FLAGS_REGISTER_zf), .S0(INSTRUCTION_COUNTER_q0), .S1(INSTRUCTION_COUNTER_q1),
    .S2(INSTRUCTION_COUNTER_q2), .IR0(IREG_q[4]), .IR1(IREG_q[5]), .IR2(IREG_q[6]), .IR3(IREG_q[7]),
    .FI(instruction_rom_1_fi), .JMP(instruction_rom_1_jmp), .CO(instruction_rom_1_co),
    .CE(instruction_rom_1_ce), .DISPLAY(instruction_rom_1_display), .BOUT(instruction_rom_1_bout),
    .BIN(instruction_rom_1_bin), .SIGNED(instruction_rom_1_signed), .S1_2(instruction_rom_1_s1_2),
    .S2_2(instruction_rom_1_s2_2), .SU(instruction_rom_1_su), .E0(instruction_rom_1_e0),
    .AOUT(instruction_rom_1_aout), .AIN(instruction_rom_1_ain), .IROUT(instruction_rom_1_irout),
    .IRLOAD(instruction_rom_1_irload), .WR(instruction_rom_1_wr), .CS(instruction_rom_1_cs),
    .MI(instruction_rom_1_mi), .HLT(instruction_rom_1_hlt));
  LED led_17 (.in(ADD_MUX_out[1]));
  LED led_18 (.in(ADD_MUX_out[0]));
  OCTALBUSTRANSCEIVER octalbustransceiver_1 (
    .D(RAM_o), .ENA(and_3_out), .Q({octalbustransceiver_1_q_2, octalbustransceiver_1_q}));
  and and_3 (and_3_out, not_1_out, instruction_rom_1_cs);
  LED led_19 (.in(RAM_o[0]));
  MUX2X1 ADD_MUX_2 (.A(MANUALDATA_sw4), .B(octalbustransceiver_1_q_2), .Select(PROGRAMMING), .Out(ADD_MUX_3_out[7:4]));
  MUX2X1 ADD_MUX_3 (.A(MANUALDATA_sw8), .B(octalbustransceiver_1_q), .Select(PROGRAMMING), .Out(ADD_MUX_3_out[3:0]));
  LED led_20 (.in(IREG_q[0]));
  LED led_21 (.in(octalbustransceiver_1_q_2[3]));
  LED led_22 (.in(octalbustransceiver_1_q_2[1]));
  LED led_23 (.in(octalbustransceiver_1_q_2[2]));
  OCTALBUSTRANSCEIVER octalbustransceiver_2 (
    .D({undriven, IREG_q[3:0]}), .ENA(instruction_rom_1_irout),
    .Q({octalbustransceiver_1_q_2, octalbustransceiver_1_q}));
  not not_2 (not_2_out, CLOCK_output);
  LED led_24 (.in(octalbustransceiver_1_q[1]));
  LED led_25 (.in(octalbustransceiver_1_q[2]));
  LED led_26 (.in(octalbustransceiver_1_q_2[0]));
  LED led_27 (.in(octalbustransceiver_1_q[3]));
  nor nor_1 (nor_1_out, octalbustransceiver_3_q[0], octalbustransceiver_3_q[1], octalbustransceiver_3_q[2], octalbustransceiver_3_q[3], octalbustransceiver_3_q[4], octalbustransceiver_3_q[5], octalbustransceiver_3_q[6], octalbustransceiver_3_q[7]);
  LED led_28 (.in(INSTRUCTION_COUNTER_q2));
  LED led_29 (.in(INSTRUCTION_COUNTER_q1));
  COUNTER4BIT INSTRUCTION_COUNTER (
    .LOAD(1'b0), .ENA(1'b1), .CLK(not_2_out), .RESET(masterreset_1_stepreset), .Q0(INSTRUCTION_COUNTER_q0),
    .Q1(INSTRUCTION_COUNTER_q1), .Q2(INSTRUCTION_COUNTER_q2));  // open: D0, D1, D2, D3, Q3
  DEMUX3X8 demux3x8_1 (
    .ENA(1'b1), .A2(INSTRUCTION_COUNTER_q2), .A1(INSTRUCTION_COUNTER_q1), .A0(INSTRUCTION_COUNTER_q0),
    .Y5(demux3x8_1_y5));  // open: Y0, Y1, Y2, Y3, Y4, Y6, Y7
  LED led_30 (.in(octalbustransceiver_1_q[0]));
  LED led_31 (.in(INSTRUCTION_COUNTER_q0));
  Button u_RESET (.out(RESET_out));
  MASTERRESET masterreset_1 (
    .in_1(RESET_out), .T5(demux3x8_1_y5), .RESET(masterreset_1_reset), .STEPRESET(masterreset_1_stepreset));
  TIMER CLOCK (.Select(Select), .Pulse(Pulse), .Hlt(instruction_rom_1_hlt), .Output(CLOCK_output));
  LED led_32 (.in(CLOCK_output));
  FLAGS_REG FLAGS_REGISTER (
    .CLK(CLOCK_output), .ENA(instruction_rom_1_fi), .CARRY(ALU_carry), .ZERO(nor_1_out),
    .RESET(masterreset_1_reset), .CF(FLAGS_REGISTER_cf), .ZF(FLAGS_REGISTER_zf));
  OCTALBUSTRANSCEIVER octalbustransceiver_3 (
    .D({octalbustransceiver_1_q_2, octalbustransceiver_1_q}), .ENA(instruction_rom_1_e0),
    .Q(octalbustransceiver_3_q));
  COUNTER4BIT PROGRAM_COUNTER (
    .LOAD(instruction_rom_1_jmp), .ENA(instruction_rom_1_ce), .CLK(CLOCK_output),
    .RESET(masterreset_1_reset), .D0(octalbustransceiver_1_q[0]), .Q0(PROGRAM_COUNTER_q0[0]),
    .D1(octalbustransceiver_1_q[1]), .Q1(PROGRAM_COUNTER_q0[1]), .D2(octalbustransceiver_1_q[2]),
    .Q2(PROGRAM_COUNTER_q0[2]), .D3(octalbustransceiver_1_q[3]), .Q3(PROGRAM_COUNTER_q0[3]));
  ALU ALU (
    .A(REG_A_q), .B(REG_B_q), .SU(instruction_rom_1_su), .S2(instruction_rom_1_s2_2),
    .S1(instruction_rom_1_s1_2), .E0(instruction_rom_1_e0), .Carry(ALU_carry),
    .Result({octalbustransceiver_1_q_2, octalbustransceiver_1_q}));
  LED led_33 (.in(PROGRAM_COUNTER_q0[1]));
  LED led_34 (.in(PROGRAM_COUNTER_q0[2]));
  LED led_35 (.in(PROGRAM_COUNTER_q0[3]));
  DREG8BIT REG_B (
    .CLEAR(masterreset_1_reset), .LOAD(instruction_rom_1_bin),
    .D({octalbustransceiver_1_q_2, octalbustransceiver_1_q}), .PAR(1'b0), .CLOCK(CLOCK_output), .Q(REG_B_q));  // open: PD
  DREG8BIT REG_A (
    .CLEAR(masterreset_1_reset), .LOAD(instruction_rom_1_ain),
    .D({octalbustransceiver_1_q_2, octalbustransceiver_1_q}), .PAR(1'b0), .CLOCK(CLOCK_output), .Q(REG_A_q));  // open: PD
  LED led_36 (.in(PROGRAM_COUNTER_q0[0]));
  LED led_37 (.in(REG_B_q[6]));
  LED led_38 (.in(REG_B_q[7]));
  LED led_39 (.in(REG_B_q[5]));
  LED led_40 (.in(REG_A_q[7]));
  LED led_41 (.in(REG_A_q[5]));
  LED led_42 (.in(REG_A_q[6]));
  LED led_43 (.in(REG_A_q[4]));
  QUATERNARYTRANSCEIVER quaternarytransceiver_1 (
    .D(PROGRAM_COUNTER_q0), .ENA(instruction_rom_1_co), .Q(octalbustransceiver_1_q));
  OCTALBUSTRANSCEIVER octalbustransceiver_4 (
    .D({octalbustransceiver_1_q_2, octalbustransceiver_1_q}), .ENA(instruction_rom_1_display),
    .Q(octalbustransceiver_4_q));
  LED led_44 (.in(REG_B_q[4]));
  LED led_45 (.in(REG_B_q[2]));
  LED led_46 (.in(REG_B_q[3]));
  LED led_47 (.in(REG_B_q[1]));
  LED led_48 (.in(REG_A_q[0]));
  LED led_49 (.in(REG_A_q[2]));
  LED led_50 (.in(REG_A_q[3]));
  LED led_51 (.in(REG_A_q[1]));
  DREG8BIT dreg8bit_1 (
    .CLEAR(masterreset_1_reset), .PD(octalbustransceiver_4_q), .PAR(instruction_rom_1_display),
    .Q(dreg8bit_1_q));  // open: LOAD, D, CLOCK
  LED led_52 (.in(REG_B_q[0]));
  OCTALBUSTRANSCEIVER octalbustransceiver_5 (
    .D(REG_A_q), .ENA(instruction_rom_1_aout), .Q({octalbustransceiver_1_q_2, octalbustransceiver_1_q}));
  BCDCONVERTER8BIT bcdconverter8bit_1 (
    .in_1(dreg8bit_1_q), .SIGNED(instruction_rom_1_signed), .Negative(bcdconverter8bit_1_negative),
    .HUNDREDS1(bcdconverter8bit_1_hundreds1), .HUNDREDS0(bcdconverter8bit_1_hundreds0),
    .TENS3(bcdconverter8bit_1_tens3), .TENS2(bcdconverter8bit_1_tens2), .TENS1(bcdconverter8bit_1_tens1),
    .TENS0(bcdconverter8bit_1_tens0), .ONES3(bcdconverter8bit_1_ones3), .ONES2(bcdconverter8bit_1_ones2),
    .ONES1(bcdconverter8bit_1_ones1), .ONES0(bcdconverter8bit_1_ones0));
  OCTALBUSTRANSCEIVER octalbustransceiver_6 (
    .D(REG_B_q), .ENA(instruction_rom_1_bout), .Q({octalbustransceiver_1_q_2, octalbustransceiver_1_q}));
  DECODER7SEGMENT decoder7segment_1 (
    .A1(bcdconverter8bit_1_hundreds1), .A0(bcdconverter8bit_1_hundreds0), .a(decoder7segment_1_a),
    .b(decoder7segment_1_b), .c(decoder7segment_1_c), .d(decoder7segment_1_d), .e(decoder7segment_1_e),
    .f(decoder7segment_1_f), .g(decoder7segment_1_g));  // open: A3, A2
  DECODER7SEGMENT decoder7segment_2 (
    .A3(bcdconverter8bit_1_tens3), .A2(bcdconverter8bit_1_tens2), .A1(bcdconverter8bit_1_tens1),
    .A0(bcdconverter8bit_1_tens0), .a(decoder7segment_2_a), .b(decoder7segment_2_b), .c(decoder7segment_2_c),
    .d(decoder7segment_2_d), .e(decoder7segment_2_e), .f(decoder7segment_2_f), .g(decoder7segment_2_g));
  DECODER7SEGMENT decoder7segment_3 (
    .A3(bcdconverter8bit_1_ones3), .A2(bcdconverter8bit_1_ones2), .A1(bcdconverter8bit_1_ones1),
    .A0(bcdconverter8bit_1_ones0), .a(decoder7segment_3_a), .b(decoder7segment_3_b), .c(decoder7segment_3_c),
    .d(decoder7segment_3_d), .e(decoder7segment_3_e), .f(decoder7segment_3_f), .g(decoder7segment_3_g));
  and and_4 (and_4_out, bcdconverter8bit_1_negative, instruction_rom_1_signed);
  _7_Segment_Display u_7_segment_display_1 (
    .g(decoder7segment_1_g), .f(decoder7segment_1_f), .a(decoder7segment_1_a), .b(decoder7segment_1_b),
    .e(decoder7segment_1_e), .d(decoder7segment_1_d), .c(decoder7segment_1_c));  // open: dp
  _7_Segment_Display u_7_segment_display_2 (.g(and_4_out));  // open: f, a, b, e, d, c, dp
  _7_Segment_Display u_7_segment_display_3 (
    .g(decoder7segment_2_g), .f(decoder7segment_2_f), .a(decoder7segment_2_a), .b(decoder7segment_2_b),
    .e(decoder7segment_2_e), .d(decoder7segment_2_d), .c(decoder7segment_2_c));  // open: dp
  _7_Segment_Display u_7_segment_display_4 (
    .g(decoder7segment_3_g), .f(decoder7segment_3_f), .a(decoder7segment_3_a), .b(decoder7segment_3_b),
    .e(decoder7segment_3_e), .d(decoder7segment_3_d), .c(decoder7segment_3_c));  // open: dp
endmodule

module TIMER (
  input  Select,
  input  Pulse,
  input  Hlt,
  output Output
);

  wire and_1_out, and_2_out, clock_1_out, not_1_out, not_2_out, or_1_out;

  Clock clock_1 (.out(clock_1_out));
  not not_1 (not_1_out, Select);
  and and_1 (and_1_out, clock_1_out, not_1_out);
  and and_2 (and_2_out, Select, Pulse);
  or or_1 (or_1_out, and_1_out, and_2_out);
  and and_3 (Output, or_1_out, not_2_out);
  not not_2 (not_2_out, Hlt);
endmodule

module DREG8BIT (
  input  PAR,
  input  [7:0] PD,
  input  CLEAR,
  input  LOAD,
  input  [7:0] D,
  input  CLOCK,
  output [7:0] Q
);

  wire and_1_out, and_2_out, and_3_out, and_4_out, and_5_out, and_6_out, and_7_out, and_8_out, and_9_out,
       and_10_out, and_11_out, and_12_out, and_13_out, and_14_out, and_15_out, and_16_out, and_17_out,
       and_18_out, and_19_out, and_20_out, and_21_out, and_22_out, and_23_out, and_24_out,
       controlled_buffer_1_out, controlled_buffer_2_out, controlled_buffer_3_out, controlled_buffer_4_out,
       controlled_buffer_5_out, controlled_buffer_6_out, controlled_buffer_7_out, controlled_buffer_8_out,
       d_ff_3_q, d_ff_3_qn, d_ff_5_q, d_ff_5_qn, d_ff_9_q, d_ff_9_qn, d_ff_11_q, d_ff_11_qn, not_1_out,
       not_2_out, not_3_out, not_4_out, not_5_out, not_6_out, not_7_out, not_8_out, or_1_out, or_2_out,
       or_3_out, or_4_out, or_5_out, or_7_out, or_9_out, or_10_out, or_11_out, or_12_out, or_13_out,
       or_15_out, undriven, undriven_2, undriven_3, undriven_4, undriven_5, undriven_6, undriven_7,
       undriven_8, undriven_9, undriven_10, undriven_11, undriven_12, undriven_13, undriven_14, undriven_15,
       undriven_16;

  not not_1 (not_1_out, LOAD);
  not not_2 (not_2_out, LOAD);
  not not_3 (not_3_out, LOAD);
  not not_4 (not_4_out, LOAD);
  not not_5 (not_5_out, LOAD);
  not not_6 (not_6_out, LOAD);
  not not_7 (not_7_out, LOAD);
  not not_8 (not_8_out, LOAD);
  and and_1 (and_1_out, Q[0], not_1_out);
  and and_2 (and_2_out, LOAD, D[0]);
  and and_3 (and_3_out, Q[1], not_2_out);
  and and_4 (and_4_out, LOAD, D[1]);
  and and_5 (and_5_out, Q[2], not_3_out);
  and and_6 (and_6_out, LOAD, D[2]);
  and and_7 (and_7_out, Q[3], not_4_out);
  and and_8 (and_8_out, LOAD, D[3]);
  and and_9 (and_9_out, Q[4], not_5_out);
  and and_10 (and_10_out, LOAD, D[4]);
  and and_11 (and_11_out, Q[5], not_6_out);
  and and_12 (and_12_out, LOAD, D[5]);
  and and_13 (and_13_out, Q[6], not_7_out);
  and and_14 (and_14_out, LOAD, D[6]);
  and and_15 (and_15_out, Q[7], not_8_out);
  and and_16 (and_16_out, LOAD, D[7]);
  D_Flip_Flop d_ff_1 (
    .D(or_1_out), .clk(CLOCK), .Q(Q[0]), .preset(controlled_buffer_1_out), .reset(or_2_out));  // open: Qn
  or or_1 (or_1_out, and_1_out, and_2_out);
  or or_2 (or_2_out, CLEAR, and_17_out);
  D_Flip_Flop d_ff_2 (
    .D(or_3_out), .clk(CLOCK), .Q(Q[1]), .preset(controlled_buffer_2_out), .reset(or_4_out));  // open: Qn
  or or_3 (or_3_out, and_3_out, and_4_out);
  or or_4 (or_4_out, CLEAR, and_18_out);
  D_Flip_Flop d_ff_3 (
    .clk(undriven), .D(undriven_2), .Q(d_ff_3_q), .Qn(d_ff_3_qn), .preset(undriven_9), .reset(undriven_13));
  D_Flip_Flop d_ff_4 (
    .clk(undriven), .D(undriven_2), .Q(d_ff_3_q), .Qn(d_ff_3_qn), .preset(undriven_9), .reset(undriven_13));
  or or_5 (or_5_out, and_5_out, and_6_out);
  // OR_Gate or_6 has open pins: in0=CLEAR, in1=and_19_out, out=open
  D_Flip_Flop d_ff_5 (
    .clk(undriven_3), .D(undriven_4), .Q(d_ff_5_q), .Qn(d_ff_5_qn), .preset(undriven_10), .reset(undriven_14));
  D_Flip_Flop d_ff_6 (
    .clk(undriven_3), .D(undriven_4), .Q(d_ff_5_q), .Qn(d_ff_5_qn), .preset(undriven_10), .reset(undriven_14));
  or or_7 (or_7_out, and_7_out, and_8_out);
  // OR_Gate or_8 has open pins: in0=CLEAR, in1=and_20_out, out=open
  D_Flip_Flop d_ff_7 (
    .D(or_9_out), .clk(CLOCK), .Q(Q[4]), .preset(controlled_buffer_5_out), .reset(or_10_out));  // open: Qn
  or or_9 (or_9_out, and_9_out, and_10_out);
  or or_10 (or_10_out, CLEAR, and_21_out);
  D_Flip_Flop d_ff_8 (
    .D(or_11_out), .clk(CLOCK), .Q(Q[5]), .preset(controlled_buffer_6_out), .reset(or_12_out));  // open: Qn
  or or_11 (or_11_out, and_11_out, and_12_out);
  or or_12 (or_12_out, CLEAR, and_22_out);
  D_Flip_Flop d_ff_9 (
    .clk(undriven_5), .D(undriven_6), .Q(d_ff_9_q), .Qn(d_ff_9_qn), .preset(undriven_11), .reset(undriven_15));
  D_Flip_Flop d_ff_10 (
    .clk(undriven_5), .D(undriven_6), .Q(d_ff_9_q), .Qn(d_ff_9_qn), .preset(undriven_11), .reset(undriven_15));
  or or_13 (or_13_out, and_13_out, and_14_out);
  // OR_Gate or_14 has open pins: in0=CLEAR, in1=and_23_out, out=open
  D_Flip_Flop d_ff_11 (
    .clk(undriven_7), .D(undriven_8), .Q(d_ff_11_q), .Qn(d_ff_11_qn), .preset(undriven_12),
    .reset(undriven_16));
  D_Flip_Flop d_ff_12 (
    .clk(undriven_7), .D(undriven_8), .Q(d_ff_11_q), .Qn(d_ff_11_qn), .preset(undriven_12),
    .reset(undriven_16));
  or or_15 (or_15_out, and_15_out, and_16_out);
  // OR_Gate or_16 has open pins: in0=CLEAR, in1=and_24_out, out=open
  assign controlled_buffer_1_out = PAR ? PD[0] : 1'bz;  // Controlled_Buffer controlled_buffer_1
  and and_17 (and_17_out, PAR, ~PD[0]);  // AND_Gate
  assign controlled_buffer_2_out = PAR ? PD[1] : 1'bz;  // Controlled_Buffer controlled_buffer_2
  and and_18 (and_18_out, PAR, ~PD[1]);  // AND_Gate
  assign controlled_buffer_3_out = PAR ? PD[2] : 1'bz;  // Controlled_Buffer controlled_buffer_3
  and and_19 (and_19_out, PAR, ~PD[2]);  // AND_Gate
  assign controlled_buffer_4_out = PAR ? PD[3] : 1'bz;  // Controlled_Buffer controlled_buffer_4
  and and_20 (and_20_out, PAR, ~PD[3]);  // AND_Gate
  assign controlled_buffer_5_out = PAR ? PD[4] : 1'bz;  // Controlled_Buffer controlled_buffer_5
  and and_21 (and_21_out, PAR, ~PD[4]);  // AND_Gate
  assign controlled_buffer_6_out = PAR ? PD[5] : 1'bz;  // Controlled_Buffer controlled_buffer_6
  and and_22 (and_22_out, PAR, ~PD[5]);  // AND_Gate
  assign controlled_buffer_7_out = PAR ? PD[6] : 1'bz;  // Controlled_Buffer controlled_buffer_7
  and and_23 (and_23_out, PAR, ~PD[6]);  // AND_Gate
  assign controlled_buffer_8_out = PAR ? PD[7] : 1'bz;  // Controlled_Buffer controlled_buffer_8
  and and_24 (and_24_out, PAR, ~PD[7]);  // AND_Gate
  Pull_Resistor pull_resistor_1 (.node(PAR));
endmodule

module OCTALBUSTRANSCEIVER (
  input  ENA,
  input  [7:0] D,
  output [7:0] Q
);

  assign Q = ENA ? D : 8'bz;  // Controlled_Buffer controlled_buffer_1
endmodule

module ALU (
  input  [7:0] A,
  input  [7:0] B,
  input  SU,
  input  S2,
  input  S1,
  input  E0,
  output Carry,
  output [7:0] Result
);

  wire not_1_out;
  wire [7:0] adder8bit_1_out, and_1_out, inverter_1_output, mux4x1_1_y, octalbustransceiver_1_q, or_1_out,
       xor_1_out;

  not not_1 (not_1_out, SU);
  INVERTER inverter_1 (.Enable(SU), .Input(B), .Output(inverter_1_output));
  OCTALBUSTRANSCEIVER octalbustransceiver_1 (.D(B), .ENA(not_1_out), .Q(octalbustransceiver_1_q));
  OCTALBUSTRANSCEIVER octalbustransceiver_2 (.D(inverter_1_output), .ENA(SU), .Q(octalbustransceiver_1_q));
  ADDER8BIT adder8bit_1 (.A(A), .B(octalbustransceiver_1_q), .Ci(SU), .Out(adder8bit_1_out), .Carry(Carry));
  assign and_1_out = A & octalbustransceiver_1_q;  // AND_Gate and_1, 8 bits wide
  assign or_1_out = A | octalbustransceiver_1_q;  // OR_Gate or_1, 8 bits wide
  assign xor_1_out = A ^ octalbustransceiver_1_q;  // XOR_Gate xor_1, 8 bits wide
  MUX4X1 mux4x1_1 (
    .I0(adder8bit_1_out), .I1(and_1_out), .I2(or_1_out), .I3(xor_1_out), .S2(S2), .S1(S1), .Y(mux4x1_1_y));
  OCTALBUSTRANSCEIVER octalbustransceiver_3 (.D(mux4x1_1_y), .ENA(E0), .Q(Result));
endmodule

module ADDER8BIT (
  input  [7:0] A,
  input  [7:0] B,
  input  Ci,
  output [7:0] Out,
  output Carry
);

  wire adder1bit_1_co, adder1bit_2_co, adder1bit_3_co, adder1bit_4_co, adder1bit_5_co, adder1bit_6_co,
       adder1bit_7_co;

  ADDER1BIT adder1bit_1 (.Ci(Ci), .A(A[0]), .B(B[0]), .Q(Out[0]), .Co(adder1bit_1_co));
  ADDER1BIT adder1bit_2 (.Ci(adder1bit_3_co), .A(A[2]), .B(B[2]), .Q(Out[2]), .Co(adder1bit_2_co));
  ADDER1BIT adder1bit_3 (.Ci(adder1bit_1_co), .A(A[1]), .B(B[1]), .Q(Out[1]), .Co(adder1bit_3_co));
  ADDER1BIT adder1bit_4 (.Ci(adder1bit_2_co), .A(A[3]), .B(B[3]), .Q(Out[3]), .Co(adder1bit_4_co));
  ADDER1BIT adder1bit_5 (.Ci(adder1bit_4_co), .A(A[4]), .B(B[4]), .Q(Out[4]), .Co(adder1bit_5_co));
  ADDER1BIT adder1bit_6 (.Ci(adder1bit_5_co), .A(A[5]), .B(B[5]), .Q(Out[5]), .Co(adder1bit_6_co));
  ADDER1BIT adder1bit_7 (.Ci(adder1bit_6_co), .A(A[6]), .B(B[6]), .Q(Out[6]), .Co(adder1bit_7_co));
  ADDER1BIT adder1bit_8 (.Ci(adder1bit_7_co), .A(A[7]), .B(B[7]), .Q(Out[7]), .Co(Carry));
endmodule

module ADDER1BIT (
  input  Ci,
  input  A,
  input  B,
  output Q,
  output Co
);

  wire and_1_out, and_2_out, xor_1_out;

  xor xor_1 (xor_1_out, A, B);
  and and_1 (and_1_out, xor_1_out, Ci);
  and and_2 (and_2_out, A, B);
  xor xor_2 (Q, xor_1_out, Ci);
  or or_1 (Co, and_1_out, and_2_out);
endmodule

module INVERTER (
  input  Enable,
  input  [7:0] Input,
  output [7:0] Output
);

  xor xor_1 (Output[1], Input[1], Enable);
  xor xor_2 (Output[0], Input[0], Enable);
  xor xor_3 (Output[2], Input[2], Enable);
  xor xor_4 (Output[3], Input[3], Enable);
  xor xor_5 (Output[4], Input[4], Enable);
  xor xor_6 (Output[5], Input[5], Enable);
  xor xor_7 (Output[6], Input[6], Enable);
  xor xor_8 (Output[7], Input[7], Enable);
endmodule

module DECODER4TO16 (
  input  D,
  input  C,
  input  B,
  input  A,
  input  ENA,
  output Y0,
  output Y1,
  output Y2,
  output Y3,
  output Y4,
  output Y5,
  output Y6,
  output Y7,
  output Y8,
  output Y9,
  output Y10,
  output Y11,
  output Y12,
  output Y13,
  output Y14,
  output Y15
);

  wire not_1_out, not_2_out, not_3_out, not_4_out;

  not not_1 (not_1_out, D);
  not not_2 (not_2_out, C);
  not not_3 (not_3_out, B);
  not not_4 (not_4_out, A);
  and and_1 (Y0, not_1_out, not_2_out, not_3_out, not_4_out, ENA);
  and and_2 (Y1, D, not_2_out, not_3_out, not_4_out, ENA);
  and and_3 (Y2, not_1_out, C, not_3_out, not_4_out, ENA);
  and and_4 (Y3, D, C, not_3_out, not_4_out, ENA);
  and and_5 (Y4, not_1_out, not_2_out, B, not_4_out, ENA);
  and and_6 (Y5, D, not_2_out, B, not_4_out, ENA);
  and and_7 (Y6, not_1_out, C, B, not_4_out, ENA);
  and and_8 (Y7, D, C, B, not_4_out, ENA);
  and and_9 (Y8, not_1_out, not_2_out, not_3_out, A, ENA);
  and and_10 (Y9, D, not_2_out, not_3_out, A, ENA);
  and and_11 (Y10, not_1_out, C, not_3_out, A, ENA);
  and and_12 (Y11, D, C, not_3_out, A, ENA);
  and and_13 (Y12, not_1_out, not_2_out, B, A, ENA);
  and and_14 (Y13, D, not_2_out, B, A, ENA);
  and and_15 (Y14, not_1_out, C, B, A, ENA);
  and and_16 (Y15, D, C, B, A, ENA);
endmodule

module RAMREG8BIT (
  input  ENA,
  input  WR,
  input  [7:0] Data,
  input  RESET,
  output [7:0] Output
);

  wire and_1_out, and_2_out, not_1_out, or_1_out, or_2_out, or_3_out, or_4_out, or_5_out, or_6_out, or_7_out,
       or_8_out;
  wire [7:0] d_ff_8_q, octalbustransceiver_1_q;

  not not_1 (not_1_out, WR);
  and and_1 (and_1_out, ENA, WR);
  and and_2 (and_2_out, ENA, not_1_out);
  OCTALBUSTRANSCEIVER octalbustransceiver_1 (.D(Data), .ENA(and_1_out), .Q(octalbustransceiver_1_q));
  D_Flip_Flop d_ff_1 (.Q(d_ff_8_q[7]), .preset(octalbustransceiver_1_q[7]), .reset(or_1_out));  // open: D, clk, Qn
  or or_1 (or_1_out, ~octalbustransceiver_1_q[7], RESET);  // OR_Gate
  OCTALBUSTRANSCEIVER octalbustransceiver_2 (.D(d_ff_8_q), .ENA(and_2_out), .Q(Output));
  D_Flip_Flop d_ff_2 (.Q(d_ff_8_q[6]), .preset(octalbustransceiver_1_q[6]), .reset(or_2_out));  // open: D, clk, Qn
  or or_2 (or_2_out, ~octalbustransceiver_1_q[6], RESET);  // OR_Gate
  D_Flip_Flop d_ff_3 (.Q(d_ff_8_q[5]), .preset(octalbustransceiver_1_q[5]), .reset(or_3_out));  // open: D, clk, Qn
  or or_3 (or_3_out, ~octalbustransceiver_1_q[5], RESET);  // OR_Gate
  D_Flip_Flop d_ff_4 (.Q(d_ff_8_q[4]), .preset(octalbustransceiver_1_q[4]), .reset(or_4_out));  // open: D, clk, Qn
  or or_4 (or_4_out, ~octalbustransceiver_1_q[4], RESET);  // OR_Gate
  D_Flip_Flop d_ff_5 (.Q(d_ff_8_q[3]), .preset(octalbustransceiver_1_q[3]), .reset(or_5_out));  // open: D, clk, Qn
  or or_5 (or_5_out, ~octalbustransceiver_1_q[3], RESET);  // OR_Gate
  D_Flip_Flop d_ff_6 (.Q(d_ff_8_q[2]), .preset(octalbustransceiver_1_q[2]), .reset(or_6_out));  // open: D, clk, Qn
  or or_6 (or_6_out, ~octalbustransceiver_1_q[2], RESET);  // OR_Gate
  D_Flip_Flop d_ff_7 (.Q(d_ff_8_q[1]), .preset(octalbustransceiver_1_q[1]), .reset(or_7_out));  // open: D, clk, Qn
  or or_7 (or_7_out, ~octalbustransceiver_1_q[1], RESET);  // OR_Gate
  D_Flip_Flop d_ff_8 (.Q(d_ff_8_q[0]), .preset(octalbustransceiver_1_q[0]), .reset(or_8_out));  // open: D, clk, Qn
  or or_8 (or_8_out, ~octalbustransceiver_1_q[0], RESET);  // OR_Gate
endmodule

module RAM16BYTE (
  input  [3:0] A,
  input  RESET,
  input  [7:0] D,
  input  WR,
  input  CS,
  output [7:0] O
);

  wire decoder4to16_1_y0, decoder4to16_1_y1, decoder4to16_1_y2, decoder4to16_1_y3, decoder4to16_1_y4,
       decoder4to16_1_y5, decoder4to16_1_y6, decoder4to16_1_y7, decoder4to16_1_y8, decoder4to16_1_y9,
       decoder4to16_1_y10, decoder4to16_1_y11, decoder4to16_1_y12, decoder4to16_1_y13, decoder4to16_1_y14,
       decoder4to16_1_y15;
  wire [7:0] ramreg8bit_1_output;

  DECODER4TO16 decoder4to16_1 (
    .D(A[0]), .C(A[1]), .B(A[2]), .A(A[3]), .ENA(1'b1), .Y0(decoder4to16_1_y0), .Y1(decoder4to16_1_y1),
    .Y2(decoder4to16_1_y2), .Y3(decoder4to16_1_y3), .Y4(decoder4to16_1_y4), .Y5(decoder4to16_1_y5),
    .Y6(decoder4to16_1_y6), .Y7(decoder4to16_1_y7), .Y8(decoder4to16_1_y8), .Y9(decoder4to16_1_y9),
    .Y10(decoder4to16_1_y10), .Y11(decoder4to16_1_y11), .Y12(decoder4to16_1_y12), .Y13(decoder4to16_1_y13),
    .Y14(decoder4to16_1_y14), .Y15(decoder4to16_1_y15));
  RAMREG8BIT ramreg8bit_1 (.ENA(decoder4to16_1_y0), .WR(WR), .Data(D), .RESET(RESET), .Output(ramreg8bit_1_output));
  RAMREG8BIT ramreg8bit_2 (.ENA(decoder4to16_1_y8), .WR(WR), .Data(D), .RESET(RESET), .Output(ramreg8bit_1_output));
  RAMREG8BIT ramreg8bit_3 (.ENA(decoder4to16_1_y1), .WR(WR), .Data(D), .RESET(RESET), .Output(ramreg8bit_1_output));
  RAMREG8BIT ramreg8bit_4 (.ENA(decoder4to16_1_y9), .WR(WR), .Data(D), .RESET(RESET), .Output(ramreg8bit_1_output));
  RAMREG8BIT ramreg8bit_5 (.ENA(decoder4to16_1_y2), .WR(WR), .Data(D), .RESET(RESET), .Output(ramreg8bit_1_output));
  RAMREG8BIT ramreg8bit_6 (.ENA(decoder4to16_1_y10), .WR(WR), .Data(D), .RESET(RESET), .Output(ramreg8bit_1_output));
  RAMREG8BIT ramreg8bit_7 (.ENA(decoder4to16_1_y3), .WR(WR), .Data(D), .RESET(RESET), .Output(ramreg8bit_1_output));
  RAMREG8BIT ramreg8bit_8 (.ENA(decoder4to16_1_y11), .WR(WR), .Data(D), .RESET(RESET), .Output(ramreg8bit_1_output));
  RAMREG8BIT ramreg8bit_9 (.ENA(decoder4to16_1_y4), .WR(WR), .Data(D), .RESET(RESET), .Output(ramreg8bit_1_output));
  RAMREG8BIT ramreg8bit_10 (.ENA(decoder4to16_1_y12), .WR(WR), .Data(D), .RESET(RESET), .Output(ramreg8bit_1_output));
  RAMREG8BIT ramreg8bit_11 (.ENA(decoder4to16_1_y5), .WR(WR), .Data(D), .RESET(RESET), .Output(ramreg8bit_1_output));
  RAMREG8BIT ramreg8bit_12 (.ENA(decoder4to16_1_y13), .WR(WR), .Data(D), .RESET(RESET), .Output(ramreg8bit_1_output));
  RAMREG8BIT ramreg8bit_13 (.ENA(decoder4to16_1_y6), .WR(WR), .Data(D), .RESET(RESET), .Output(ramreg8bit_1_output));
  RAMREG8BIT ramreg8bit_14 (.ENA(decoder4to16_1_y14), .WR(WR), .Data(D), .RESET(RESET), .Output(ramreg8bit_1_output));
  RAMREG8BIT ramreg8bit_15 (.ENA(decoder4to16_1_y7), .WR(WR), .Data(D), .RESET(RESET), .Output(ramreg8bit_1_output));
  RAMREG8BIT ramreg8bit_16 (.ENA(decoder4to16_1_y15), .WR(WR), .Data(D), .RESET(RESET), .Output(ramreg8bit_1_output));
  OCTALBUSTRANSCEIVER octalbustransceiver_1 (.D(ramreg8bit_1_output), .ENA(CS), .Q(O));
endmodule

module MUX4X1 (
  input  S2,
  input  S1,
  input  [7:0] I0,
  input  [7:0] I1,
  input  [7:0] I2,
  input  [7:0] I3,
  output [7:0] Y
);

  wire not_1_out, not_2_out;
  wire [7:0] and_1_out, and_2_out, and_3_out, and_4_out, bit_extender_1_out, bit_extender_2_out,
       bit_extender_3_out, bit_extender_4_out;

  not not_1 (not_1_out, S2);
  assign bit_extender_1_out = {{7{not_1_out}}, not_1_out};  // Bit_Extender bit_extender_1
  assign bit_extender_2_out = {{7{S2}}, S2};  // Bit_Extender bit_extender_2
  not not_2 (not_2_out, S1);
  assign bit_extender_3_out = {{7{not_2_out}}, not_2_out};  // Bit_Extender bit_extender_3
  assign bit_extender_4_out = {{7{S1}}, S1};  // Bit_Extender bit_extender_4
  assign and_1_out = bit_extender_3_out & I0 & bit_extender_1_out;  // AND_Gate and_1, 8 bits wide
  assign and_2_out = bit_extender_4_out & I1 & bit_extender_1_out;  // AND_Gate and_2, 8 bits wide
  assign and_3_out = bit_extender_3_out & I2 & bit_extender_2_out;  // AND_Gate and_3, 8 bits wide
  assign and_4_out = bit_extender_4_out & I3 & bit_extender_2_out;  // AND_Gate and_4, 8 bits wide
  assign Y = and_1_out | and_2_out | and_3_out | and_4_out;  // OR_Gate or_1, 8 bits wide
endmodule

module MUX2X1 (
  input  [3:0] A,
  input  [3:0] B,
  input  Select,
  output [3:0] Out
);

  wire [3:0] and_1_out, and_2_out, bit_extender_1_out, not_1_out;

  assign not_1_out = ~bit_extender_1_out;  // NOT_Gate not_1, 4 bits wide
  assign bit_extender_1_out = {{3{Select}}, Select};  // Bit_Extender bit_extender_1
  assign and_1_out = A & bit_extender_1_out;  // AND_Gate and_1, 4 bits wide
  assign and_2_out = B & not_1_out;  // AND_Gate and_2, 4 bits wide
  assign Out = and_1_out | and_2_out;  // OR_Gate or_1, 4 bits wide
endmodule

module MEMREG4BIT (
  input  CLEAR,
  input  LOAD,
  input  [3:0] D,
  input  CLOCK,
  output [3:0] Q
);

  wire and_1_out, and_2_out, and_3_out, and_4_out, and_5_out, and_6_out, and_7_out, and_8_out, d_ff_3_q,
       d_ff_3_qn, d_ff_5_q, d_ff_5_qn, not_1_out, not_2_out, not_3_out, not_4_out, or_1_out, or_2_out,
       or_3_out, or_4_out, undriven, undriven_2, undriven_3, undriven_4, undriven_5, undriven_6, undriven_7,
       undriven_8;

  not not_1 (not_1_out, LOAD);
  not not_2 (not_2_out, LOAD);
  not not_3 (not_3_out, LOAD);
  not not_4 (not_4_out, LOAD);
  and and_1 (and_1_out, Q[0], not_1_out);
  and and_2 (and_2_out, LOAD, D[0]);
  and and_3 (and_3_out, Q[1], not_2_out);
  and and_4 (and_4_out, LOAD, D[1]);
  and and_5 (and_5_out, Q[2], not_3_out);
  and and_6 (and_6_out, LOAD, D[2]);
  and and_7 (and_7_out, Q[3], not_4_out);
  and and_8 (and_8_out, LOAD, D[3]);
  D_Flip_Flop d_ff_1 (.D(or_1_out), .clk(CLOCK), .Q(Q[0]), .reset(CLEAR));  // open: Qn, preset
  or or_1 (or_1_out, and_1_out, and_2_out);
  D_Flip_Flop d_ff_2 (.D(or_2_out), .clk(CLOCK), .Q(Q[1]), .reset(CLEAR));  // open: Qn, preset
  or or_2 (or_2_out, and_3_out, and_4_out);
  D_Flip_Flop d_ff_3 (
    .clk(undriven), .D(undriven_2), .Q(d_ff_3_q), .Qn(d_ff_3_qn), .preset(undriven_5), .reset(undriven_7));
  D_Flip_Flop d_ff_4 (
    .clk(undriven), .D(undriven_2), .Q(d_ff_3_q), .Qn(d_ff_3_qn), .preset(undriven_5), .reset(undriven_7));
  or or_3 (or_3_out, and_5_out, and_6_out);
  D_Flip_Flop d_ff_5 (
    .clk(undriven_3), .D(undriven_4), .Q(d_ff_5_q), .Qn(d_ff_5_qn), .preset(undriven_6), .reset(undriven_8));
  D_Flip_Flop d_ff_6 (
    .clk(undriven_3), .D(undriven_4), .Q(d_ff_5_q), .Qn(d_ff_5_qn), .preset(undriven_6), .reset(undriven_8));
  or or_4 (or_4_out, and_7_out, and_8_out);
endmodule

module COUNTER4BIT (
  input  D0,
  input  D1,
  input  D2,
  input  D3,
  input  LOAD,
  input  ENA,
  input  CLK,
  input  RESET,
  output Q0,
  output Q1,
  output Q2,
  output Q3
);

  wire and_1_out, and_2_out, and_3_out, and_4_out, and_5_out, and_6_out, and_7_out, or_1_out, or_2_out,
       or_3_out, or_4_out;

  and and_1 (and_1_out, LOAD, ~D0);  // AND_Gate
  COUNTER1BIT counter1bit_1 (.ENA(ENA), .CLK(CLK), .LOAD(LOAD), .DATA(D0), .RESET(or_1_out), .Q(Q0));
  or or_1 (or_1_out, and_1_out, RESET);
  COUNTER1BIT counter1bit_2 (.ENA(and_2_out), .CLK(CLK), .LOAD(LOAD), .DATA(D1), .RESET(or_2_out), .Q(Q1));
  and and_2 (and_2_out, Q0, ENA);
  or or_2 (or_2_out, and_3_out, RESET);
  and and_3 (and_3_out, LOAD, ~D1);  // AND_Gate
  and and_4 (and_4_out, Q1, and_2_out);
  or or_3 (or_3_out, and_5_out, RESET);
  and and_5 (and_5_out, LOAD, ~D2);  // AND_Gate
  COUNTER1BIT counter1bit_3 (.ENA(and_4_out), .CLK(CLK), .LOAD(LOAD), .DATA(D2), .RESET(or_3_out), .Q(Q2));
  and and_6 (and_6_out, Q2, and_4_out);
  and and_7 (and_7_out, LOAD, ~D3);  // AND_Gate
  COUNTER1BIT counter1bit_4 (.ENA(and_6_out), .CLK(CLK), .LOAD(LOAD), .DATA(D3), .RESET(or_4_out), .Q(Q3));
  or or_4 (or_4_out, and_7_out, RESET);
endmodule

module COUNTER1BIT (
  input  LOAD,
  input  DATA,
  input  ENA,
  input  CLK,
  input  RESET,
  output Q
);

  wire and_1_out, and_2_out, and_3_out, j_k_ff_1_qn;

  and and_1 (and_1_out, j_k_ff_1_qn, ENA);
  and and_2 (and_2_out, ENA, Q);
  and and_3 (and_3_out, LOAD, DATA);
  J_K_Flip_Flop j_k_ff_1 (
    .J(and_1_out), .K(and_2_out), .clk(CLK), .Q(Q), .Qn(j_k_ff_1_qn), .preset(and_3_out), .reset(RESET));
endmodule

module QUATERNARYTRANSCEIVER (
  input  ENA,
  input  [3:0] D,
  output [3:0] Q
);

  assign Q = ENA ? D : 4'bz;  // Controlled_Buffer controlled_buffer_1
endmodule

module MODULO5 (
  input  A3,
  input  A2,
  input  A1,
  input  A0,
  output S3,
  output S2,
  output S1,
  output S0
);

  wire and_1_out, and_2_out, and_3_out, and_4_out, and_5_out, and_6_out, and_7_out, and_8_out, and_9_out,
       and_10_out, and_11_out, and_12_out, and_13_out, and_14_out, not_1_out, not_2_out, not_3_out, not_4_out;

  not not_1 (not_1_out, A3);
  not not_2 (not_2_out, A2);
  not not_3 (not_3_out, A0);
  not not_4 (not_4_out, A1);
  and and_1 (and_1_out, A0, A2);
  and and_2 (and_2_out, A1, A2);
  and and_3 (and_3_out, not_3_out, not_4_out, A2, not_1_out);
  and and_4 (and_4_out, A0, not_4_out, not_2_out, A3);
  and and_5 (and_5_out, not_3_out, A1, A2, A3);
  and and_6 (and_6_out, A1, not_2_out, not_1_out);
  and and_7 (and_7_out, not_4_out, A2, A3);
  and and_8 (and_8_out, A0, A1, A2, not_1_out);
  and and_9 (and_9_out, not_3_out, not_4_out, not_2_out, A3);
  and and_10 (and_10_out, A0, not_2_out, not_1_out);
  and and_11 (and_11_out, A0, A1, not_2_out, A3);
  and and_12 (and_12_out, A0, not_4_out, A2, A3);
  and and_13 (and_13_out, not_3_out, A1, A2, not_1_out);
  and and_14 (and_14_out, not_3_out, not_4_out, not_2_out, A3);
  or or_1 (S3, A3, and_1_out, and_2_out);
  or or_2 (S2, and_3_out, and_4_out, and_5_out);
  or or_3 (S1, and_6_out, and_7_out, and_8_out, and_9_out);
  or or_4 (S0, and_10_out, and_11_out, and_12_out, and_13_out, and_14_out);
endmodule

module BCDCONVERTER8BIT (
  input  [7:0] in_1,
  input  SIGNED,
  output HUNDREDS1,
  output HUNDREDS0,
  output Negative,
  output TENS3,
  output TENS2,
  output TENS1,
  output TENS0,
  output ONES3,
  output ONES2,
  output ONES1,
  output ONES0
);

  wire modulo5_1_s0, modulo5_1_s1, modulo5_1_s2, modulo5_1_s3, modulo5_2_s0, modulo5_2_s1, modulo5_2_s2,
       modulo5_2_s3, modulo5_3_s0, modulo5_3_s1, modulo5_3_s2, modulo5_3_s3, modulo5_4_s0, modulo5_4_s1,
       modulo5_4_s2, modulo5_4_s3, modulo5_6_s0, modulo5_6_s1, modulo5_6_s2, not_1_out;
  wire [7:0] adder8bit_1_out, bit_extender_1_out, inverter_1_output, octalbustransceiver_1_q;
  wire [7:1] octalbustransceiver_2_q;

  and and_1 (Negative, in_1[7], SIGNED);
  OCTALBUSTRANSCEIVER octalbustransceiver_1 (.D(in_1), .ENA(SIGNED), .Q(octalbustransceiver_1_q));
  INVERTER inverter_1 (.Enable(in_1[7]), .Input(octalbustransceiver_1_q), .Output(inverter_1_output));
  assign bit_extender_1_out = {{7{1'b0}}, 1'b0};  // Bit_Extender bit_extender_1
  ADDER8BIT adder8bit_1 (
    .A(inverter_1_output), .B(bit_extender_1_out), .Ci(SIGNED), .Out(adder8bit_1_out));  // open: Carry
  not not_1 (not_1_out, Negative);
  OCTALBUSTRANSCEIVER octalbustransceiver_2 (.D(in_1), .ENA(not_1_out), .Q({octalbustransceiver_2_q, ONES0}));
  OCTALBUSTRANSCEIVER octalbustransceiver_3 (.D(adder8bit_1_out), .ENA(Negative), .Q({octalbustransceiver_2_q, ONES0}));
  MODULO5 modulo5_1 (
    .A3(1'b0), .A2(octalbustransceiver_2_q[7]), .A1(octalbustransceiver_2_q[6]),
    .A0(octalbustransceiver_2_q[5]), .S3(modulo5_1_s3), .S2(modulo5_1_s2), .S1(modulo5_1_s1),
    .S0(modulo5_1_s0));
  MODULO5 modulo5_2 (
    .A3(modulo5_1_s2), .A2(modulo5_1_s1), .A1(modulo5_1_s0), .A0(octalbustransceiver_2_q[4]),
    .S3(modulo5_2_s3), .S2(modulo5_2_s2), .S1(modulo5_2_s1), .S0(modulo5_2_s0));
  MODULO5 modulo5_3 (
    .A3(modulo5_2_s2), .A2(modulo5_2_s1), .A1(modulo5_2_s0), .A0(octalbustransceiver_2_q[3]),
    .S3(modulo5_3_s3), .S2(modulo5_3_s2), .S1(modulo5_3_s1), .S0(modulo5_3_s0));
  MODULO5 modulo5_4 (
    .A3(modulo5_3_s2), .A2(modulo5_3_s1), .A1(modulo5_3_s0), .A0(octalbustransceiver_2_q[2]),
    .S3(modulo5_4_s3), .S2(modulo5_4_s2), .S1(modulo5_4_s1), .S0(modulo5_4_s0));
  MODULO5 modulo5_5 (
    .A3(modulo5_4_s2), .A2(modulo5_4_s1), .A1(modulo5_4_s0), .A0(octalbustransceiver_2_q[1]), .S3(TENS0),
    .S2(ONES3), .S1(ONES2), .S0(ONES1));
  MODULO5 modulo5_6 (
    .A3(1'b0), .A2(modulo5_1_s3), .A1(modulo5_2_s3), .A0(modulo5_3_s3), .S3(HUNDREDS1), .S2(modulo5_6_s2),
    .S1(modulo5_6_s1), .S0(modulo5_6_s0));
  MODULO5 modulo5_7 (
    .A3(modulo5_6_s2), .A2(modulo5_6_s1), .A1(modulo5_6_s0), .A0(modulo5_4_s3), .S3(HUNDREDS0), .S2(TENS3),
    .S1(TENS2), .S0(TENS1));
endmodule

module DECODER7SEGMENT (
  input  A3,
  input  A2,
  input  A1,
  input  A0,
  output a,
  output b,
  output c,
  output d,
  output e,
  output f,
  output g
);

  wire and_1_out, and_2_out, and_3_out, and_4_out, and_5_out, and_6_out, and_7_out, and_8_out, and_9_out,
       and_10_out, and_11_out, and_12_out, and_13_out, and_14_out, and_15_out, and_16_out, not_1_out,
       not_2_out, not_3_out;

  not not_1 (not_1_out, A2);
  not not_2 (not_2_out, A1);
  not not_3 (not_3_out, A0);
  and and_1 (and_1_out, A2, A0);
  and and_2 (and_2_out, not_1_out, not_3_out);
  and and_3 (and_3_out, A0, A1);
  and and_4 (and_4_out, not_3_out, not_2_out);
  and and_5 (and_5_out, not_3_out, not_1_out);
  and and_6 (and_6_out, A1, not_1_out);
  and and_7 (and_7_out, not_3_out, A1);
  and and_8 (and_8_out, A0, not_2_out, A2);
  and and_9 (and_9_out, not_3_out, not_1_out);
  and and_10 (and_10_out, not_3_out, A1);
  and and_11 (and_11_out, not_3_out, A2);
  and and_12 (and_12_out, not_3_out, not_2_out);
  and and_13 (and_13_out, not_2_out, A2);
  and and_14 (and_14_out, not_1_out, A1);
  and and_15 (and_15_out, A2, not_2_out);
  and and_16 (and_16_out, A1, not_3_out);
  or or_1 (a, A3, A1, and_1_out, and_2_out);
  or or_2 (b, not_1_out, and_3_out, and_4_out);
  or or_3 (c, not_2_out, A0, A2);
  or or_4 (d, A3, and_5_out, and_6_out, and_7_out, and_8_out);
  or or_5 (e, and_9_out, and_10_out);
  or or_6 (f, and_11_out, and_12_out, and_13_out, A3);
  or or_7 (g, and_14_out, and_15_out, and_16_out, A3);
endmodule

module DEMUX3X8 (
  input  A2,
  input  A1,
  input  A0,
  input  ENA,
  output Y0,
  output Y1,
  output Y2,
  output Y3,
  output Y4,
  output Y5,
  output Y6,
  output Y7
);

  wire not_1_out, not_2_out, not_3_out;

  not not_1 (not_1_out, A2);
  not not_2 (not_2_out, A1);
  not not_3 (not_3_out, A0);
  and and_1 (Y0, not_3_out, not_2_out, not_1_out, ENA);
  and and_2 (Y1, A0, not_2_out, not_1_out, ENA);
  and and_3 (Y2, not_3_out, A1, not_1_out, ENA);
  and and_4 (Y3, A0, A1, not_1_out, ENA);
  and and_5 (Y4, not_3_out, not_2_out, A2, ENA);
  and and_6 (Y5, A0, not_2_out, A2, ENA);
  and and_7 (Y6, not_3_out, A1, A2, ENA);
  and and_8 (Y7, A0, A1, A2, ENA);
endmodule

module MASTERRESET (
  input  in_1,
  input  T5,
  output RESET,
  output STEPRESET
);

  or or_1 (STEPRESET, in_1, T5);

  assign RESET = in_1;
endmodule

module FLAGS_REG (
  input  CLK,
  input  ENA,
  input  CARRY,
  input  ZERO,
  input  RESET,
  output CF,
  output ZF
);

  wire and_1_out, and_2_out, and_3_out, and_4_out, not_1_out, or_1_out, or_2_out;

  not not_1 (not_1_out, ENA);
  and and_1 (and_1_out, CF, not_1_out);
  and and_2 (and_2_out, CARRY, ENA);
  and and_3 (and_3_out, ZF, not_1_out);
  and and_4 (and_4_out, ZERO, ENA);
  D_Flip_Flop u_CARRY (.D(or_1_out), .clk(CLK), .Q(CF), .reset(RESET));  // open: Qn, preset
  or or_1 (or_1_out, and_1_out, and_2_out);
  D_Flip_Flop u_ZERO (.D(or_2_out), .clk(CLK), .Q(ZF), .reset(RESET));  // open: Qn, preset
  or or_2 (or_2_out, and_3_out, and_4_out);
endmodule
