// Logisim project INSTRUCTION_ROM.circ as structural Verilog: 1 circuit, main circuit INSTRUCTION_ROM
module INSTRUCTION_ROM (
  input  CF,
  input  ZF,
  input  S0,
  input  S1,
  input  S2,
  input  IR0,
  input  IR1,
  input  IR2,
  input  IR3,
  output FI,
  output JMP,
  output CO,
  output CE,
  output DISPLAY,
  output BOUT,
  output BIN,
  output SIGNED,
  output S1_2,
  output S2_2,
  output SU,
  output E0,
  output AOUT,
  output AIN,
  output IROUT,
  output IRLOAD,
  output WR,
  output CS,
  output MI,
  output HLT
);

  ROM #(.addrWidth(9), .dataWidth(20)) rom_1 (
    .addr({IR3, IR2, IR1, IR0, S2, S1, S0, ZF, CF}),
    .data({HLT, MI, CS, WR, IRLOAD, IROUT, AIN, AOUT, E0, SU, S2_2, S1_2, SIGNED, BIN, BOUT, DISPLAY, CE, CO, JMP, FI}));

  // Notes on the sheet:
  //   contents of rom_1 (hex, n*v repeats v):
  //   40004 40004 40004 40004 28008 28008 28008 28008 24*0 40004 40004 40004 40004 28008 28008 28008 28008
  //   44000 22000 22000 22000 22000 19*0 40004 40004 40004 40004 28008 28008 28008 28008 44000 20040 2801
  //   2801 2801 2801 18*0 40004 40004 40004 40004 28008 28008 28008 28008 44000 20040 2c01 2c01 2c01 2c01
  //   18*0 40004 40004 40004 40004 28008 28008 28008 28008 44000 22000 22000 22000 22000 19*0 40004 40004
  //   40004 40004 28008 28008 28008 28008 6000 6000 6000 6000 20*0 40004 40004 40004 40004 28008 28008
  //   28008 28008 4002 4002 4002 4002 20*0 40004 40004 40004 40004 28008 28008 28008 28008 24*0 40004
  //   40004 40004 40004 28008 28008 28008 28008 24*0 40004 40004 40004 40004 28008 28008 28008 28008 24*0
  //   40004 40004 40004 40004 28008 28008 28008 28008 24*0 40004 40004 40004 40004 28008 28008 28008 28008
  //   24*0 40004 40004 40004 40004 28008 28008 28008 28008 24*0 40004 40004 40004 40004 28008 28008 28008
  //   28008 24*0 40004 40004 40004 40004 28008 28008 28008 28008 1010 1010 1010 1010 28*0 80000 80000
  //   80000 80000
endmodule
